# Fritzing sketch miduino (saved by Fritzing 0.9.3b)
breadboards: 1

parts:
  Composant1 = Arduino Leonardo (Rev3b)
  S1 = Pushbutton [package="[THT]"]
  S2 = Pushbutton [package="[THT]"]
  R1 = Rotary Potentiometer (Small) [maximum_resistance=100kΩ package=THT]
  R2 = Rotary Potentiometer (Small) [maximum_resistance=100kΩ package=THT]
  S3 = Pushbutton [package="[THT]"]
  J1 = Dagu DGServo 9g header (male) [package=THT]
  J2 = Dagu DGServo 9g header (male) [package=THT]
  J3 = Infrared Proximity Sensor
  hc-sr1 = hc-sr04

nets:
  N1: Composant1.D2/SDA, S1.Pin_1, S1.Pin_2
  N2: Composant1.D3_PWM/SCL, S2.Pin_1, S2.Pin_2
  N3: Composant1.D4/A6, S3.Pin_1, S3.Pin_2
  N4: Composant1.D5_PWM, J3.Vout
  N5: Composant1.D6_PWM/A7, hc-sr1.Trig
  N6: Composant1.D7, hc-sr1.Echo
  VCC: Composant1.5V, R1.leg1, R2.leg1, J1.Vcc, J2.Vcc, J3.Vcc, hc-sr1.VCC
  GND: Composant1.GND, S1.Pin_3, S1.Pin_4, S2.Pin_3, S2.Pin_4, R1.leg2, R2.leg2, S3.Pin_3, S3.Pin_4, J1.gnd, J2.gnd, J3.GND, hc-sr1.GND
  N7: Composant1.A0, R2.wiper
  N8: Composant1.A1, R1.wiper
  N9: Composant1.D12/A11, J2.pulse
  N10: Composant1.D13_PWM, J1.pulse

notes:
  Led Strip 1
  Led Strip 2
